# Fritzing sketch STMto7segment (saved by Fritzing 0.9.4)
circuit board: 8.46667cm x 5.64444cm
breadboards: 1

parts:
  Part1 = BluePill
  7_Segment2 = 7 Segment Display
  R1 = Resistor [tolerance=±5% resistance=220 package=THT]
  R2 = Resistor [tolerance=±5% resistance=220 package=THT]
  R3 = Resistor [tolerance=±5% resistance=220 package=THT]
  R4 = Resistor [tolerance=±5% resistance=220 package=THT]
  R5 = Resistor [tolerance=±5% resistance=220 package=THT]
  R6 = Resistor [tolerance=±5% resistance=220 package=THT]
  R7 = Resistor [tolerance=±5% resistance=220 package=THT]

nets:
  N1: Part1.A0, R1.Pin_1
  N2: Part1.A1, R7.Pin_1
  N3: Part1.A3, R4.Pin_0
  N4: Part1.A4, R5.Pin_0
  N5: Part1.A5, R3.Pin_0
  N6: Part1.A6, R2.Pin_0
  N7: Part1.GND3, 7_Segment2.common_cathode
  N8: Part1.A2, R6.Pin_1
  N9: 7_Segment2.Segment_E, R5.Pin_1
  N10: 7_Segment2.Segment_D, R4.Pin_1
  N11: 7_Segment2.Segment_C, R6.Pin_0
  N12: 7_Segment2.Segment_B, R7.Pin_0
  N13: 7_Segment2.Segment_A, R1.Pin_0
  N14: 7_Segment2.Segment_F, R3.Pin_1
  N15: 7_Segment2.Segment_G, R2.Pin_1
